# Fritzing sketch senseo-api-board-example (saved by Fritzing 0.9.3b)
breadboards: 1

parts:
  Raspberry_Pi_1 = Raspberry Pi 3 [part_number=RPI-3-V1.2]
  S3 = Pushbutton [package="[THT]"]
  LED1 = LED - 5mm [color="Red (633nm)" package="5 mm [THT]"]
  Composant1 = I2C level shifter bidirectional
  S2 = Pushbutton [package="[THT]"]
  S1 = Pushbutton [part_number="Power ON" package="[THT]"]
  Composant2 = Adafruit T-Cobbler Plus [part_number="Adafruit #1989 and #2028"]  # not connected

nets:
  GND: Raspberry_Pi_1.GND, S3.Pin_3, S3.Pin_4, LED1.cathode, Composant1.GND, S2.Pin_3, S2.Pin_4, S1.Pin_3, S1.Pin_4
  N1: S3.Pin_1, S3.Pin_2, Composant1.HV3
  N2: Composant1.HV1, S1.Pin_2
  N3: Composant1.HV2, S2.Pin_1, S2.Pin_2

notes:
  Power ON
  1 mug
  2 mugs

custom parts:
  Adafruit T-Cobbler Plus: The Raspberry Pi has landed on the Maker World like a 40-GPIO pinned, quad-USB ported, credit card sized bomb of DIY joy. And while you can use most of our great Model B accessories by hooking up our downgrade cable, its probably a good time to upgrade your set up and accessorize using all of the 40 pins. That's why we now carry the Assembled Adafruit Pi T-Cobbler Plus - Breakout + Cable for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
